// Logisim project ControlUnit.circ as structural Verilog: 1 circuit, main circuit ControlUnit
module ControlUnit (
  input  [5:0] in_1,
  input  [5:0] in_2,
  output out_3,
  output out_4,
  output out_5,
  output out_6,
  output out_7,
  output out_8,
  output out_9,
  output out_10,
  output [3:0] out_11
);

  wire main_decoder_1_p3, main_decoder_1_p4;

  not not_1 (out_3, main_decoder_1_p3);
  // Main_Decoder main_decoder_1: pin names not known; wires that end beside it: out_4, in_1, main_decoder_1_p3, main_decoder_1_p4, out_5, out_6, out_7, out_8, out_9, out_10
  // ALU_Decoder alu_decoder_1: pin names not known; wires that end beside it: in_2, main_decoder_1_p4, out_11
endmodule
