// Logisim project MIPS.circ as structural Verilog: 2 circuits, main circuit main
module main (
);

  wire and_1_out, buff_32_1_out_2, CLK, comparator_1_eq, hazard_unit_1_p2, hazard_unit_1_p3,
       hazard_unit_1_p4, hazard_unit_1_p5, hazard_unit_1_p6, hazard_unit_1_p9, hazard_unit_1_p11,
       hazard_unit_1_p13, hazard_unit_1_p18, hazard_unit_1_p19, hazard_unit_1_p20, not_1_out,
       reg_stage2_1_alusrce, reg_stage2_1_memwritee, reg_stage2_1_regdste, reg_stage3_1_memtoregm,
       reg_stage4_1_memtoregw, undriven, undriven_2, undriven_3, undriven_4, undriven_5, undriven_6,
       undriven_8;
  wire [1:0] hazard_unit_1_p15, hazard_unit_1_p16;
  wire [3:0] adder_1_out_2, reg_stage2_1_aluctrle, undriven_7;
  wire [4:0] hazard_unit_1_p10, hazard_unit_1_p12, hazard_unit_1_p14, hazard_unit_1_p17, hazard_unit_1_p21,
       reg_stage2_1_rde;
  wire [27:0] adder_1_out, bit_extender_1_out, shifter_1_out;
  wire [31:0] adder_2_out, alu_1_alu_result, bit_extender_2_out, datamem_1_p5, instmem_1_out_2,
       multiplexer_1_out, multiplexer_2_out, multiplexer_3_out, multiplexer_4_out, multiplexer_6_out,
       multiplexer_7_out, multiplexer_8_out, multiplexer_9_out, PC_q, reg_stage1_1_instrd,
       reg_stage1_1_pcplus4d, reg_stage2_1_signimme, reg_stage2_1_srcae, reg_stage2_1_srcbe,
       reg_stage3_1_aluoutm, reg_stage3_1_writedatam, reg_stage4_1_aluoutw, reg_stage4_1_readdataw,
       regfile32_1_rd1, regfile32_1_rd2, shifter_2_out;

  Clock clock_1 (.out(CLK));
  Multiplexer #(.width(32)) multiplexer_1 (
    .in0({adder_1_out_2, adder_1_out}), .in1(adder_2_out), .out(multiplexer_1_out), .sel(and_1_out));  // open: en
  // Hazard_Unit hazard_unit_1: pin names not known; wires that end beside it: CLK, hazard_unit_1_p2, hazard_unit_1_p3, hazard_unit_1_p4, hazard_unit_1_p5, hazard_unit_1_p6, reg_stage1_1_instrd[25:21], reg_stage1_1_instrd[20:16], hazard_unit_1_p9, hazard_unit_1_p10, hazard_unit_1_p11, hazard_unit_1_p12, hazard_unit_1_p13, hazard_unit_1_p14, hazard_unit_1_p15, hazard_unit_1_p16, hazard_unit_1_p17, hazard_unit_1_p18, hazard_unit_1_p19, hazard_unit_1_p20, hazard_unit_1_p21
  Multiplexer #(.width(32)) multiplexer_2 (
    .in0(multiplexer_1_out), .in1({adder_1_out_2, shifter_1_out}), .out(multiplexer_2_out), .sel(undriven));  // open: en
  Register #(.width(32)) PC (.D(multiplexer_2_out), .en(not_1_out), .Q(PC_q), .clk(CLK));  // open: clr
  not not_1 (not_1_out, hazard_unit_1_p2);
  Adder #(.width(32)) adder_1 (.a(PC_q), .b(32'h4), .out({adder_1_out_2, adder_1_out}));  // open: cin, cout
  Reg_Stage1 reg_stage1_1 (
    .CLR(and_1_out), .EN(hazard_unit_1_p3), .CLK(CLK), .InstrF(instmem_1_out_2),
    .PCPlus4F({adder_1_out_2, adder_1_out}), .InstrD(reg_stage1_1_instrd), .PCPlus4D(reg_stage1_1_pcplus4d));
  InstMem instmem_1 (.A(PC_q), .out_2(instmem_1_out_2));
  assign bit_extender_1_out = {{2{reg_stage1_1_instrd[25]}}, reg_stage1_1_instrd[25:0]};  // Bit_Extender bit_extender_1
  // ControlUnit controlunit_1: pin names not known
  Buff_32 buff_32_1 (.in_1(CLK), .out_2(buff_32_1_out_2));
  assign bit_extender_2_out = {{16{reg_stage1_1_instrd[15]}}, reg_stage1_1_instrd[15:0]};  // Bit_Extender bit_extender_2
  Shifter #(.width(28)) shifter_1 (.in(bit_extender_1_out), .\dist (5'b00010), .out(shifter_1_out));
  RegFile32 regfile32_1 (
    .AD1(reg_stage1_1_instrd[25:21]), .AD2(reg_stage1_1_instrd[20:16]), .CLK(buff_32_1_out_2),
    .WE(hazard_unit_1_p20), .AD3(hazard_unit_1_p21), .WD3(multiplexer_9_out), .RD1(regfile32_1_rd1),
    .RD2(regfile32_1_rd2));
  Shifter #(.width(32)) shifter_2 (.in(bit_extender_2_out), .\dist (5'b00010), .out(shifter_2_out));
  and and_1 (and_1_out, undriven_8, comparator_1_eq, hazard_unit_1_p6);
  Comparator #(.width(32)) comparator_1 (
    .a(multiplexer_3_out), .b(multiplexer_4_out), .eq(comparator_1_eq));  // open: gt, lt
  Adder #(.width(32)) adder_2 (.a(shifter_2_out), .b(reg_stage1_1_pcplus4d), .out(adder_2_out));  // open: cin, cout
  Multiplexer #(.width(32)) multiplexer_3 (
    .in0(regfile32_1_rd1), .in1(reg_stage3_1_aluoutm), .out(multiplexer_3_out), .sel(hazard_unit_1_p4));  // open: en
  Multiplexer #(.width(32)) multiplexer_4 (
    .in0(regfile32_1_rd2), .in1(reg_stage3_1_aluoutm), .out(multiplexer_4_out), .sel(hazard_unit_1_p5));  // open: en
  Reg_Stage2 reg_stage2_1 (
    .CLK(CLK), .CLR(hazard_unit_1_p9), .MemtoRegD(undriven_2), .MemWriteD(undriven_3), .ALUSrcD(undriven_4),
    .RegDstD(undriven_5), .RegWriteD(undriven_6), .ALUCtrlD(undriven_7), .SrcAD(regfile32_1_rd1),
    .SrcBD(regfile32_1_rd2), .RsD(reg_stage1_1_instrd[25:21]), .RtD(reg_stage1_1_instrd[20:16]),
    .RdD(reg_stage1_1_instrd[15:11]), .SignImmD(bit_extender_2_out), .MemtoRegE(hazard_unit_1_p11),
    .MemWriteE(reg_stage2_1_memwritee), .ALUSrcE(reg_stage2_1_alusrce), .RegDstE(reg_stage2_1_regdste),
    .RegWriteE(hazard_unit_1_p13), .ALUCtrlE(reg_stage2_1_aluctrle), .SrcAE(reg_stage2_1_srcae),
    .SrcBE(reg_stage2_1_srcbe), .RsE(hazard_unit_1_p10), .RtE(hazard_unit_1_p12), .RdE(reg_stage2_1_rde),
    .SignImmE(reg_stage2_1_signimme));
  Multiplexer #(.width(5)) multiplexer_5 (
    .in0(hazard_unit_1_p12), .in1(reg_stage2_1_rde), .out(hazard_unit_1_p14), .sel(reg_stage2_1_regdste));  // open: en
  Multiplexer #(.width(32)) multiplexer_6 (
    .in0(reg_stage2_1_srcbe), .in1(reg_stage2_1_signimme), .out(multiplexer_6_out), .sel(reg_stage2_1_alusrce));  // open: en
  Multiplexer #(.select(2), .width(32)) multiplexer_7 (
    .in0(reg_stage2_1_srcae), .in1(reg_stage3_1_aluoutm), .in2(multiplexer_9_out), .out(multiplexer_7_out),
    .sel(hazard_unit_1_p15));  // open: in3, en
  Multiplexer #(.select(2), .width(32)) multiplexer_8 (
    .in0(multiplexer_6_out), .in1(reg_stage3_1_aluoutm), .in2(multiplexer_9_out), .out(multiplexer_8_out),
    .sel(hazard_unit_1_p16));  // open: in3, en
  Reg_Stage3 reg_stage3_1 (
    .RegWriteE(hazard_unit_1_p11), .MemtoRegE(reg_stage2_1_memwritee), .MemWriteE(hazard_unit_1_p13),
    .ALUOutE(alu_1_alu_result), .WriteDataE(reg_stage2_1_srcbe), .WriteRegE(hazard_unit_1_p14),
    .RegWriteM(hazard_unit_1_p19), .MemtoRegM(reg_stage3_1_memtoregm), .MemWriteM(hazard_unit_1_p18),
    .ALUOutM(reg_stage3_1_aluoutm), .WriteDataM(reg_stage3_1_writedatam), .WriteRegM(hazard_unit_1_p17),
    .CLK(CLK));
  ALU alu_1 (
    .SrcA(multiplexer_7_out), .SrcB(multiplexer_8_out), .ALU_Control(reg_stage2_1_aluctrle),
    .ALU_Result(alu_1_alu_result));  // open: Zero
  Reg_Stage4 reg_stage4_1 (
    .CLK(CLK), .RegWriteM(hazard_unit_1_p18), .MemtoRegM(hazard_unit_1_p19), .ALUOutM(reg_stage3_1_aluoutm),
    .ReadDataM(datamem_1_p5), .WriteRegM(hazard_unit_1_p17), .RegWriteW(hazard_unit_1_p20),
    .MemtoRegW(reg_stage4_1_memtoregw), .ALUOutW(reg_stage4_1_aluoutw), .ReadDataW(reg_stage4_1_readdataw),
    .WriteRegW(hazard_unit_1_p21));
  // DataMem datamem_1: pin names not known; wires that end beside it: reg_stage3_1_aluoutm, reg_stage3_1_writedatam, CLK, reg_stage3_1_memtoregm, datamem_1_p5
  Multiplexer #(.width(32)) multiplexer_9 (
    .in0(reg_stage4_1_aluoutw), .in1(reg_stage4_1_readdataw), .out(multiplexer_9_out),
    .sel(reg_stage4_1_memtoregw));  // open: en
endmodule

module Buff_32 (
  input  in_1,
  output out_2
);

  wire buffer_1_out, buffer_2_out, buffer_3_out, buffer_4_out, buffer_5_out, buffer_6_out, buffer_7_out,
       buffer_8_out, buffer_9_out, buffer_10_out, buffer_11_out, buffer_12_out, buffer_13_out, buffer_14_out,
       buffer_15_out, buffer_16_out, buffer_17_out, buffer_18_out, buffer_19_out, buffer_20_out,
       buffer_21_out, buffer_22_out, buffer_23_out, buffer_24_out, buffer_25_out, buffer_26_out,
       buffer_27_out, buffer_28_out, buffer_29_out, buffer_30_out, buffer_31_out;

  buf buffer_1 (buffer_1_out, in_1);
  buf buffer_2 (buffer_2_out, buffer_1_out);
  buf buffer_3 (buffer_3_out, buffer_5_out);
  buf buffer_4 (buffer_4_out, buffer_2_out);
  buf buffer_5 (buffer_5_out, buffer_6_out);
  buf buffer_6 (buffer_6_out, buffer_4_out);
  buf buffer_7 (buffer_7_out, buffer_9_out);
  buf buffer_8 (buffer_8_out, buffer_3_out);
  buf buffer_9 (buffer_9_out, buffer_8_out);
  buf buffer_10 (buffer_10_out, buffer_7_out);
  buf buffer_11 (buffer_11_out, buffer_14_out);
  buf buffer_12 (buffer_12_out, buffer_13_out);
  buf buffer_13 (buffer_13_out, buffer_11_out);
  buf buffer_14 (buffer_14_out, buffer_10_out);
  buf buffer_15 (buffer_15_out, buffer_12_out);
  buf buffer_16 (buffer_16_out, buffer_15_out);
  buf buffer_17 (buffer_17_out, buffer_18_out);
  buf buffer_18 (buffer_18_out, buffer_16_out);
  buf buffer_19 (buffer_19_out, buffer_20_out);
  buf buffer_20 (buffer_20_out, buffer_22_out);
  buf buffer_21 (buffer_21_out, buffer_19_out);
  buf buffer_22 (buffer_22_out, buffer_17_out);
  buf buffer_23 (buffer_23_out, buffer_24_out);
  buf buffer_24 (buffer_24_out, buffer_21_out);
  buf buffer_25 (buffer_25_out, buffer_23_out);
  buf buffer_26 (buffer_26_out, buffer_25_out);
  buf buffer_27 (buffer_27_out, buffer_29_out);
  buf buffer_28 (buffer_28_out, buffer_30_out);
  buf buffer_29 (buffer_29_out, buffer_26_out);
  buf buffer_30 (buffer_30_out, buffer_27_out);
  buf buffer_31 (buffer_31_out, buffer_28_out);
  buf buffer_32 (out_2, buffer_31_out);
endmodule
